// Logisim project module-logic-design.circ as structural Verilog: 3 circuits, main circuit main
module main (
  input  pedal,
  input  pedal_2,
  input  pedal_3,
  input  pedal_4,
  input  pedal_5,
  output PEDALS,
  output [3:0] COUNT,
  output [3:0] COUNT_2
);

  wire and_1_out, CLK_2_out, CLK_out, pedal_module_1_clk_2, pedal_module_1_gnd_2, pedal_module_1_nw_s,
       pedal_module_1_pedal_out, pedal_module_1_vcc_2, pedal_module_2_clk_2, pedal_module_2_gnd_2,
       pedal_module_2_nw_s, pedal_module_2_pedal_out, pedal_module_2_sys_pedals, pedal_module_2_vcc_2,
       pedal_module_2_vcc_prev, pedal_module_3_clk_2, pedal_module_3_gnd_2, pedal_module_3_nw_s,
       pedal_module_3_pedal_out, pedal_module_3_sys_pedals, pedal_module_3_vcc_2, pedal_module_3_vcc_prev,
       pedal_module_4_clk_2, pedal_module_4_gnd_2, pedal_module_4_nw_s, pedal_module_4_pedal_out,
       pedal_module_4_sys_pedals, pedal_module_4_vcc_2, pedal_module_4_vcc_prev, pedal_module_5_sys_pedals,
       pedal_module_5_vcc_prev, variable_oscillator_1_nwrite___shift;
  wire [3:0] pedal_module_1_count_out, pedal_module_2_count_out, pedal_module_2_sys_count,
       pedal_module_3_count_out, pedal_module_3_sys_count, pedal_module_4_count_out,
       pedal_module_4_sys_count, pedal_module_5_sys_count;

  Clock CLK (.out(CLK_out));
  Variable_Oscillator variable_oscillator_1 (
    .CLK(CLK_out), .COUNT(COUNT), .nWRITE___SHIFT(variable_oscillator_1_nwrite___shift));
  Pedal_Module pedal_module_1 (
    .CLK(CLK_out), .nWRITE___SHIFT(variable_oscillator_1_nwrite___shift), .VCC(1'b1),
    .pedal_OUT(pedal_module_1_pedal_out), .count_OUT(pedal_module_1_count_out), .pedal(pedal),
    .sys_COUNT(COUNT), .VCC_next(pedal_module_2_vcc_prev), .sys_COUNT_in(pedal_module_2_sys_count),
    .sys_PEDALS(PEDALS), .sys_PEDALS_in(pedal_module_2_sys_pedals), .nW_S(pedal_module_1_nw_s),
    .VCC_2(pedal_module_1_vcc_2), .CLK_2(pedal_module_1_clk_2), .GND(1'b0), .GND_2(pedal_module_1_gnd_2));  // open: pedal_IN, count_IN, VCC_prev
  Clock #(.highDuration(20), .lowDuration(80)) CLK_2 (.out(CLK_2_out));
  Pedal_Module pedal_module_2 (
    .CLK(pedal_module_1_clk_2), .nWRITE___SHIFT(pedal_module_1_nw_s), .pedal_IN(pedal_module_1_pedal_out),
    .VCC(pedal_module_1_vcc_2), .count_IN(pedal_module_1_count_out), .pedal_OUT(pedal_module_2_pedal_out),
    .count_OUT(pedal_module_2_count_out), .pedal(pedal_2), .sys_COUNT(pedal_module_2_sys_count),
    .VCC_next(pedal_module_3_vcc_prev), .sys_COUNT_in(pedal_module_3_sys_count),
    .VCC_prev(pedal_module_2_vcc_prev), .sys_PEDALS(pedal_module_2_sys_pedals),
    .sys_PEDALS_in(pedal_module_3_sys_pedals), .nW_S(pedal_module_2_nw_s), .VCC_2(pedal_module_2_vcc_2),
    .CLK_2(pedal_module_2_clk_2), .GND(pedal_module_1_gnd_2), .GND_2(pedal_module_2_gnd_2));
  Pedal_Module pedal_module_3 (
    .CLK(pedal_module_2_clk_2), .nWRITE___SHIFT(pedal_module_2_nw_s), .pedal_IN(pedal_module_2_pedal_out),
    .VCC(pedal_module_2_vcc_2), .count_IN(pedal_module_2_count_out), .pedal_OUT(pedal_module_3_pedal_out),
    .count_OUT(pedal_module_3_count_out), .pedal(pedal_3), .sys_COUNT(pedal_module_3_sys_count),
    .VCC_next(pedal_module_4_vcc_prev), .sys_COUNT_in(pedal_module_4_sys_count),
    .VCC_prev(pedal_module_3_vcc_prev), .sys_PEDALS(pedal_module_3_sys_pedals),
    .sys_PEDALS_in(pedal_module_4_sys_pedals), .nW_S(pedal_module_3_nw_s), .VCC_2(pedal_module_3_vcc_2),
    .CLK_2(pedal_module_3_clk_2), .GND(pedal_module_2_gnd_2), .GND_2(pedal_module_3_gnd_2));
  Shift_Register #(.length(5)) shift_register_1 (
    .shift(variable_oscillator_1_nwrite___shift), .in(PEDALS), .clk(CLK_out));  // open: out, load, clr, d0, q0, d1, q1, d2, q2, d3, q3, d4, q4
  buf and_1 (and_1_out, CLK_2_out);  // AND_Gate
  Pedal_Module pedal_module_4 (
    .CLK(pedal_module_3_clk_2), .nWRITE___SHIFT(pedal_module_3_nw_s), .pedal_IN(pedal_module_3_pedal_out),
    .VCC(pedal_module_3_vcc_2), .count_IN(pedal_module_3_count_out), .pedal_OUT(pedal_module_4_pedal_out),
    .count_OUT(pedal_module_4_count_out), .pedal(pedal_4), .sys_COUNT(pedal_module_4_sys_count),
    .VCC_next(pedal_module_5_vcc_prev), .sys_COUNT_in(pedal_module_5_sys_count),
    .VCC_prev(pedal_module_4_vcc_prev), .sys_PEDALS(pedal_module_4_sys_pedals),
    .sys_PEDALS_in(pedal_module_5_sys_pedals), .nW_S(pedal_module_4_nw_s), .VCC_2(pedal_module_4_vcc_2),
    .CLK_2(pedal_module_4_clk_2), .GND(pedal_module_3_gnd_2), .GND_2(pedal_module_4_gnd_2));
  Pedal_Module pedal_module_5 (
    .CLK(pedal_module_4_clk_2), .nWRITE___SHIFT(pedal_module_4_nw_s), .pedal_IN(pedal_module_4_pedal_out),
    .VCC(pedal_module_4_vcc_2), .count_IN(pedal_module_4_count_out), .pedal(pedal_5),
    .sys_COUNT(pedal_module_5_sys_count), .VCC_prev(pedal_module_5_vcc_prev),
    .sys_PEDALS(pedal_module_5_sys_pedals), .GND(pedal_module_4_gnd_2));  // open: pedal_OUT, count_OUT, VCC_next, sys_COUNT_in, sys_PEDALS_in, nW_S, VCC_2, CLK_2, GND_2

  assign COUNT_2 = COUNT;

  // Notes on the sheet:
  //   Outputs from RPi
  //   Inputs to RPi
  //   VCC
  //   GND
  //   Debug outputs
  //   Pedals Serial Signal
endmodule

module Pedal_Module (
  input  pedal,
  input  VCC,
  input  CLK,
  input  nWRITE___SHIFT,
  input  pedal_IN,
  input  VCC_next,
  input  [3:0] count_IN,
  input  [3:0] sys_COUNT_in,
  input  sys_PEDALS_in,
  input  GND,
  output VCC_2,
  output CLK_2,
  output nW_S,
  output pedal_OUT,
  output VCC_prev,
  output [3:0] count_OUT,
  output [3:0] sys_COUNT,
  output sys_PEDALS,
  output GND_2
);

  wire nand_1_out, nand_2_out, nand_3_out, nand_4_out, not_1_out, not_3_out, not_4_out;
  wire [3:3] not_2_out;

  Pull_Resistor pull_resistor_1 (.node(pedal_IN));
  not not_1 (not_1_out, nWRITE___SHIFT);
  not not_2 (not_2_out[3], VCC);
  Pull_Resistor pull_resistor_2 (.node(count_IN[0]));
  Pull_Resistor pull_resistor_3 (.node(count_IN[1]));
  Pull_Resistor pull_resistor_4 (.node(count_IN[2]));
  Pull_Resistor pull_resistor_5 (.node(count_IN[3]));
  nand nand_1 (nand_1_out, nWRITE___SHIFT, pedal_IN);
  nand nand_2 (nand_2_out, not_1_out, pedal);
  Adder #(.width(4)) adder_1 (.a(count_IN), .b({4{not_2_out[3]}}), .out(count_OUT), .cin(VCC));  // open: cout
  Multiplexer #(.disabled(0), .enable("false")) multiplexer_1 (
    .in0(sys_COUNT_in[0]), .in1(count_OUT[0]), .out(sys_COUNT[0]), .sel(not_4_out));
  Multiplexer #(.disabled(0), .enable("false")) multiplexer_2 (
    .in0(sys_COUNT_in[1]), .in1(count_OUT[1]), .out(sys_COUNT[1]), .sel(not_4_out));
  Multiplexer #(.disabled(0), .enable("false")) multiplexer_3 (
    .in0(sys_COUNT_in[2]), .in1(count_OUT[2]), .out(sys_COUNT[2]), .sel(not_4_out));
  Multiplexer #(.disabled(0), .enable("false")) multiplexer_4 (
    .in0(sys_COUNT_in[3]), .in1(count_OUT[3]), .out(sys_COUNT[3]), .sel(not_4_out));
  nand nand_3 (nand_3_out, nand_1_out, nand_2_out);
  not not_3 (not_3_out, VCC_next);
  nand nand_4 (nand_4_out, VCC, not_3_out);
  not not_4 (not_4_out, nand_4_out);
  Multiplexer #(.disabled(0), .enable("false")) multiplexer_5 (
    .in0(sys_PEDALS_in), .in1(pedal_OUT), .out(sys_PEDALS), .sel(not_4_out));
  D_Flip_Flop d_ff_1 (.clk(CLK), .D(nand_3_out), .Q(pedal_OUT));  // open: Qn, preset, en, reset
  Pull_Resistor pull_resistor_6 (.node(sys_COUNT_in[0]));
  Pull_Resistor pull_resistor_7 (.node(sys_COUNT_in[1]));
  Pull_Resistor pull_resistor_8 (.node(sys_COUNT_in[2]));
  Pull_Resistor pull_resistor_9 (.node(VCC_next));
  Pull_Resistor pull_resistor_10 (.node(sys_COUNT_in[3]));
  Pull_Resistor pull_resistor_11 (.node(sys_PEDALS_in));

  assign CLK_2 = CLK;
  assign GND_2 = GND;
  assign nW_S = nWRITE___SHIFT;
  assign VCC_2 = VCC;
  assign VCC_prev = VCC;
endmodule

module Variable_Oscillator (
  input  CLK,
  input  [3:0] COUNT,
  output nWRITE___SHIFT
);

  wire d_ff_1_q, multiplexer_1_out, multiplexer_2_out, multiplexer_3_out, multiplexer_4_out, nor_1_out;
  wire [3:0] d_ff_2_q, subtractor_1_out;

  Multiplexer #(.enable("false")) multiplexer_1 (
    .in0(subtractor_1_out[0]), .in1(COUNT[0]), .out(multiplexer_1_out), .sel(nor_1_out));
  Multiplexer #(.enable("false")) multiplexer_2 (
    .in0(subtractor_1_out[1]), .in1(COUNT[1]), .out(multiplexer_2_out), .sel(nor_1_out));
  Multiplexer #(.enable("false")) multiplexer_3 (
    .in0(subtractor_1_out[2]), .in1(COUNT[2]), .out(multiplexer_3_out), .sel(nor_1_out));
  Multiplexer #(.enable("false")) multiplexer_4 (
    .in0(subtractor_1_out[3]), .in1(COUNT[3]), .out(multiplexer_4_out), .sel(nor_1_out));
  D_Flip_Flop d_ff_1 (.clk(nor_1_out), .D(nWRITE___SHIFT), .Q(d_ff_1_q));  // open: Qn, preset, en, reset
  D_Flip_Flop d_ff_2 (.clk(CLK), .D(multiplexer_1_out), .Q(d_ff_2_q[0]));  // open: Qn, preset, en, reset
  D_Flip_Flop d_ff_3 (.clk(CLK), .D(multiplexer_2_out), .Q(d_ff_2_q[1]));  // open: Qn, preset, en, reset
  D_Flip_Flop d_ff_4 (.clk(CLK), .D(multiplexer_3_out), .Q(d_ff_2_q[2]));  // open: Qn, preset, en, reset
  D_Flip_Flop d_ff_5 (.clk(CLK), .D(multiplexer_4_out), .Q(d_ff_2_q[3]));  // open: Qn, preset, en, reset
  not not_1 (nWRITE___SHIFT, d_ff_1_q);
  // Probe on subtractor_1_out
  Subtractor #(.width(4)) subtractor_1 (.a(d_ff_2_q), .b(4'b0000), .out(subtractor_1_out), .bin(1'b1));  // open: bout
  nor nor_1 (nor_1_out, subtractor_1_out[0], subtractor_1_out[1], subtractor_1_out[2], subtractor_1_out[3]);
endmodule
