# Fritzing sketch pedalsWiring_breadboard (saved by Fritzing 0.9.3b)
breadboards: 1

parts:
  Raspberry_Pi_Zero1 = Raspberry Pi Zero
  S1 = Toggle Switch [package=THT]
  IC3 = IC, DIP package, 16 pins [chip_label=Adder part_number=‎CD74HC283E‎]
  SN54HC1 = IC, DIP package, 16 pins [chip_label=Muxes part_number=SN54HC157]
  SN54HC2 = IC, DIP package, 16 pins [chip_label=Muxes part_number=SN54HC157]
  IC5 = IC, DIP package, 14 pins [chip_label=NANDs]
  IC2 = IC, DIP package, 14 pins [chip_label=Inverters]
  R1 = Resistor [tolerance=±5% resistance=10k package=THT]
  R2 = Resistor [tolerance=±5% resistance=10k package=THT]
  R3 = Resistor [tolerance=±5% resistance=10k package=THT]
  R4 = Resistor [tolerance=±5% resistance=10k package=THT]
  R11 = Resistor [tolerance=±5% resistance=10k package=THT]
  count_IN = female pin header, 4 pins [form="♀ (female)"]
  sys_pedals_OUT = male pin header, 1 pin [form="♂ (male)"]
  sys_count_OUT = male pin header, 4 pins [form="♂ (male)"]
  VCC_prev = male pin header, 1 pin [form="♂ (male)"]
  CLK_in = female pin header, 1 pin [form="♀ (female)"]
  ~W/S_in = female pin header, 1 pin [form="♀ (female)"]
  pedal_IN = female pin header, 1 pin [form="♀ (female)"]
  count_OUT = male pin header, 4 pins [form="♂ (male)"]
  VCC_in = female pin header, 1 pin [form="♀ (female)"]
  sys_count_IN = female pin header, 4 pins [form="♀ (female)"]
  sys_pedals_IN = female pin header, 1 pin [form="♀ (female)"]
  CLK_out = male pin header, 1 pin [form="♂ (male)"]
  ~W/S_out = male pin header, 1 pin [form="♂ (male)"]
  pedal_OUT = male pin header, 1 pin [form="♂ (male)"]
  GND_in = female pin header, 1 pin [form="♀ (female)"]
  R12 = Resistor [tolerance=±5% resistance=10k package=THT]
  GND_out = male pin header, 1 pin [form="♂ (male)"]
  R13 = Resistor [tolerance=±5% resistance=10k package=THT]
  R14 = Resistor [tolerance=±5% resistance=10k package=THT]
  R15 = Resistor [tolerance=±5% resistance=10k package=THT]
  R16 = Resistor [tolerance=±5% resistance=10k package=THT]
  R17 = Resistor [tolerance=±5% resistance=10k package=THT]
  VCC_out = male pin header, 1 pin [form="♂ (male)"]
  R18 = Resistor [tolerance=±5% resistance=10k package=THT]
  R19 = Resistor [tolerance=±5% resistance=10k package=THT]
  R20 = Resistor [tolerance=±5% resistance=10k package=THT]
  R21 = Resistor [tolerance=±5% resistance=10k package=THT]
  R22 = Resistor [tolerance=±5% resistance=10k package=THT]
  IC4 = IC, DIP package, 14 pins [chip_label="Flip Flop"]
  VCC_next = female pin header, 1 pin [form="♀ (female)"]

nets (from the schematic view):
  GND: Raspberry_Pi_Zero1.GND, S1.L1, IC3.pin8, SN54HC1.pin8, SN54HC2.pin8, IC5.pin7, IC2.pin7, R1.Pin_0, R2.Pin_1, R3.Pin_1, R4.Pin_0, R11.Pin_0, GND_in.pin1, R12.Pin_0, GND_out.pin1, R14.Pin_0, R15.Pin_0, R17.Pin_0, R18.Pin_0, R19.Pin_0, R22.Pin_0, IC4.pin7
  sys pedals OUT: Raspberry_Pi_Zero1.GPIO9, SN54HC1.pin4, sys_pedals_OUT.pin1
  CLK: Raspberry_Pi_Zero1.GPIO11, CLK_in.pin1, CLK_out.pin1, IC4.pin3
  sys count OUT 0: Raspberry_Pi_Zero1.GPIO5, SN54HC2.pin4, sys_count_OUT.pin1
  sys count OUT 1: Raspberry_Pi_Zero1.GPIO6, SN54HC2.pin7, sys_count_OUT.pin2
  sys count OUT 3: Raspberry_Pi_Zero1.GPIO13, SN54HC2.pin12, sys_count_OUT.pin4
  sys count OUT 2: Raspberry_Pi_Zero1.GPIO12, SN54HC2.pin9, sys_count_OUT.pin3
  ~WRITE / SHIFT: Raspberry_Pi_Zero1.GPIO8, IC5.pin2, IC2.pin1, R11.Pin_1, ~W/S_in.pin1, ~W/S_out.pin1
  5V/VCC/VCC prev: Raspberry_Pi_Zero1.5V, S1.L2, IC3.pin7, IC3.pin16, SN54HC1.pin16, SN54HC2.pin16, IC5.pin10, IC5.pin14, IC2.pin14, VCC_prev.pin1, VCC_in.pin1, VCC_out.pin1, IC4.pin14
  PEDAL: S1.COM, IC5.pin1
  count OUT 1: IC3.pin1, SN54HC2.pin6, count_OUT.pin2
  N1: IC3.pin2, R4.Pin_1
  count IN 1: IC3.pin3, count_IN.pin2
  count OUT 0: IC3.pin4, SN54HC2.pin3, count_OUT.pin1
  count IN 0: IC3.pin5, count_IN.pin1
  N2: IC3.pin6, R1.Pin_1
  count OUT 3: IC3.pin10, SN54HC2.pin13, count_OUT.pin4
  N3: IC3.pin11, R2.Pin_0
  count IN 3: IC3.pin12, count_IN.pin4, R21.Pin_1
  count OUT 2: IC3.pin13, SN54HC2.pin10, count_OUT.pin3
  count IN 2: IC3.pin14, count_IN.pin3, R20.Pin_1
  to MUXES: SN54HC1.pin1, SN54HC2.pin1, IC2.pin6
  sys pedals IN: SN54HC1.pin2, sys_pedals_IN.pin1, R12.Pin_1
  pedal OUT: SN54HC1.pin3, pedal_OUT.pin1, IC4.pin5
  sys count IN 0: SN54HC2.pin2, sys_count_IN.pin1, R14.Pin_1
  sys count IN 1: SN54HC2.pin5, sys_count_IN.pin2, R15.Pin_1
  sys count IN 2: SN54HC2.pin11, sys_count_IN.pin3, R16.Pin_1
  sys count IN 3: SN54HC2.pin14, sys_count_IN.pin4, R13.Pin_1
  to FF A: IC5.pin3, IC5.pin13
  pedal IN: IC5.pin4, pedal_IN.pin1, R22.Pin_1
  WRITE / ~SHIFT: IC5.pin5, IC2.pin2
  to FF B: IC5.pin6, IC5.pin12
  ~to MUXES: IC5.pin8, IC2.pin5
  ~VCC next: IC5.pin9, IC2.pin4
  N4: IC5.pin11, IC4.pin2
  VCC next: IC2.pin3, R17.Pin_1, VCC_next.pin1
  N5: R13.Pin_0, R16.Pin_0
