# Fritzing sketch pedalsAssembly_layer3 (saved by Fritzing 0.9.3b)
perfboards: 2

parts:
  S1 = Toggle Switch [package=THT]  # not connected
  IC3 = IC, DIP package, 16 pins [chip_label=Adder part_number=‎CD74HC283E‎]  # not connected
  SN54HC1 = IC, DIP package, 16 pins [chip_label=Muxes part_number=SN54HC157]  # not connected
  SN54HC2 = IC, DIP package, 16 pins [chip_label=Muxes part_number=SN54HC157]  # not connected
  IC5 = IC, DIP package, 14 pins [chip_label=NANDs]  # not connected
  IC4 = IC, DIP package, 14 pins [chip_label="Flip Flop"]  # not connected
  IC2 = IC, DIP package, 14 pins [chip_label=Inverters]  # not connected
  R1 = Resistor [tolerance=±5% resistance=10k package=THT]  # not connected
  R2 = Resistor [tolerance=±5% resistance=10k package=THT]  # not connected
  R3 = Resistor [tolerance=±5% resistance=10k package=THT]  # not connected
  R4 = Resistor [tolerance=±5% resistance=10k package=THT]  # not connected
  R11 = Resistor [tolerance=±5% resistance=10k package=THT]  # not connected
  count_IN = female pin header, 4 pins [form="♀ (female)"]  # not connected
  sys_pedals_OUT = male pin header, 1 pin [form="♂ (male)"]  # not connected
  sys_count_OUT = male pin header, 4 pins [form="♂ (male)"]  # not connected
  VCC_prev = male pin header, 1 pin [form="♂ (male)"]  # not connected
  CLK_in = female pin header, 1 pin [form="♀ (female)"]  # not connected
  ~W/S_in = female pin header, 1 pin [form="♀ (female)"]  # not connected
  pedal_IN = female pin header, 1 pin [form="♀ (female)"]  # not connected
  count_OUT = male pin header, 4 pins [form="♂ (male)"]  # not connected
  VCC_in = female pin header, 1 pin [form="♀ (female)"]  # not connected
  sys_count_IN = female pin header, 4 pins [form="♀ (female)"]  # not connected
  sys_pedals_IN = female pin header, 1 pin [form="♀ (female)"]  # not connected
  CLK_out = male pin header, 1 pin [form="♂ (male)"]  # not connected
  ~W/S_out = male pin header, 1 pin [form="♂ (male)"]  # not connected
  pedal_OUT = male pin header, 1 pin [form="♂ (male)"]  # not connected
  VCC_next = male pin header, 1 pin [form="♂ (male)"]  # not connected
  GND_in = female pin header, 1 pin [form="♀ (female)"]  # not connected
  R12 = Resistor [tolerance=±5% resistance=10k package=THT]  # not connected
  GND_out = male pin header, 1 pin [form="♂ (male)"]  # not connected
  R13 = Resistor [tolerance=±5% resistance=10k package=THT]  # not connected
  R14 = Resistor [tolerance=±5% resistance=10k package=THT]  # not connected
  R15 = Resistor [tolerance=±5% resistance=10k package=THT]  # not connected
  R16 = Resistor [tolerance=±5% resistance=10k package=THT]  # not connected
  R17 = Resistor [tolerance=±5% resistance=10k package=THT]  # not connected
  VCC_out = male pin header, 1 pin [form="♂ (male)"]  # not connected
  R18 = Resistor [tolerance=±5% resistance=10k package=THT]  # not connected
  R19 = Resistor [tolerance=±5% resistance=10k package=THT]  # not connected
  R20 = Resistor [tolerance=±5% resistance=10k package=THT]  # not connected
  R21 = Resistor [tolerance=±5% resistance=10k package=THT]  # not connected
  R22 = Resistor [tolerance=±5% resistance=10k package=THT]  # not connected
  GND_in1 = female pin header, 1 pin [form="♀ (female)"]  # not connected
  GND_out1 = male pin header, 1 pin [form="♂ (male)"]  # not connected
  R23 = Resistor [tolerance=±5% resistance=10k package=THT]
  R24 = Resistor [tolerance=±5% resistance=10k package=THT]
  R25 = Resistor [tolerance=±5% resistance=10k package=THT]
  sys_count_IN_B = female pin header, 4 pins [form="♀ (female)"]  # not connected
  CLK_in1 = female pin header, 1 pin [form="♀ (female)"]  # not connected
  R26 = Resistor [tolerance=±5% resistance=10k package=THT]
  R27 = Resistor [tolerance=±5% resistance=10k package=THT]
  R28 = Resistor [tolerance=±5% resistance=10k package=THT]
  IC6 = IC, DIP package, 14 pins [chip_label=Inverters]
  IC7 = IC, DIP package, 14 pins [chip_label="Flip Flop"]
  IC8 = IC, DIP package, 14 pins [chip_label=NANDs]
  SN54HC3 = IC, DIP package, 16 pins [chip_label=Muxes part_number=SN54HC157]
  IC9 = IC, DIP package, 16 pins [chip_label=Adder part_number=‎CD74HC283E‎]
  R29 = Resistor [tolerance=±5% resistance=10k package=THT]
  R30 = Resistor [tolerance=±5% resistance=10k package=THT]
  VCC_out_B = male pin header, 1 pin [form="♂ (male)"]
  R31 = Resistor [tolerance=±5% resistance=10k package=THT]
  VCC_prev1 = male pin header, 1 pin [form="♂ (male)"]
  R32 = Resistor [tolerance=±5% resistance=10k package=THT]
  SN54HC4 = IC, DIP package, 16 pins [chip_label=Muxes part_number=SN54HC157]
  R33 = Resistor [tolerance=±5% resistance=10k package=THT]
  R34 = Resistor [tolerance=±5% resistance=10k package=THT]
  CLK_out_B = male pin header, 1 pin [form="♂ (male)"]  # not connected
  sys_count_OUT_B = male pin header, 4 pins [form="♂ (male)"]  # not connected
  S2 = Toggle Switch [package=THT]
  R35 = Resistor [tolerance=±5% resistance=10k package=THT]
  pedal_OUT_B = male pin header, 1 pin [form="♂ (male)"]  # not connected
  ~W/S_out_B = male pin header, 1 pin [form="♂ (male)"]  # not connected
  sys_pedals_IN_B = female pin header, 1 pin [form="♀ (female)"]  # not connected
  R36 = Resistor [tolerance=±5% resistance=10k package=THT]
  R37 = Resistor [tolerance=±5% resistance=10k package=THT]
  pedal_IN_B = female pin header, 1 pin [form="♀ (female)"]  # not connected
  ~W/S_in1 = female pin header, 1 pin [form="♀ (female)"]  # not connected
  R38 = Resistor [tolerance=±5% resistance=10k package=THT]
  sys_pedals_OUT_B = male pin header, 1 pin [form="♂ (male)"]  # not connected
  VCC_next_B = male pin header, 1 pin [form="♂ (male)"]  # not connected
  VCC_in_B = female pin header, 1 pin [form="♀ (female)"]
  count_OUT_B = male pin header, 4 pins [form="♂ (male)"]  # not connected
  count_IN_B = female pin header, 4 pins [form="♀ (female)"]  # not connected
  GND_out_B = male pin header, 2 pins [form="♂ (male)"]  # not connected
  GND_in_B = male pin header, 2 pins [form="♂ (male)"]

nets:
  N1: R23.Pin_1, R24.Pin_1, R25.Pin_1, R26.Pin_1, R27.Pin_1, R28.Pin_1, IC6.pin1, IC7.pin1, IC8.pin1, SN54HC3.pin1, IC9.pin1, R29.Pin_1, R30.Pin_1, R31.Pin_1, R32.Pin_1, SN54HC4.pin1, R33.Pin_1, R34.Pin_1, S2.L2, R35.Pin_1, R36.Pin_1, R37.Pin_1, R38.Pin_1, GND_in_B.pin2
  N2: R26.Pin_0, IC9.pin3
  N3: R27.Pin_0, IC9.pin14
  N4: R28.Pin_0, IC9.pin7
  N5: IC6.pin8, IC7.pin4, IC7.pin7, IC7.pin8, IC7.pin9, IC7.pin10, IC7.pin11, IC7.pin12, IC8.pin12, SN54HC3.pin9, IC9.pin2, IC9.pin9, VCC_out_B.pin1, SN54HC4.pin9, S2.L1
  N6: IC8.pin8, VCC_prev1.pin1, VCC_in_B.pin1
  N7: IC9.pin10, R32.Pin_0
