# Fritzing sketch pedalsAssembly_layer4 (saved by Fritzing 0.9.3b)
perfboards: 2

parts:
  S1 = Toggle Switch [package=THT]  # not connected
  IC3 = IC, DIP package, 16 pins [chip_label=Adder part_number=‎CD74HC283E‎]
  SN54HC1 = IC, DIP package, 16 pins [chip_label=Muxes part_number=SN54HC157]  # not connected
  SN54HC2 = IC, DIP package, 16 pins [chip_label=Muxes part_number=SN54HC157]  # not connected
  IC5 = IC, DIP package, 14 pins [chip_label=NANDs]
  IC4 = IC, DIP package, 14 pins [chip_label="Flip Flop"]
  IC2 = IC, DIP package, 14 pins [chip_label=Inverters]  # not connected
  R1 = Resistor [tolerance=±5% resistance=10k package=THT]  # not connected
  R2 = Resistor [tolerance=±5% resistance=10k package=THT]  # not connected
  R3 = Resistor [tolerance=±5% resistance=10k package=THT]  # not connected
  R4 = Resistor [tolerance=±5% resistance=10k package=THT]  # not connected
  R11 = Resistor [tolerance=±5% resistance=10k package=THT]  # not connected
  count_IN = female pin header, 4 pins [form="♀ (female)"]
  sys_pedals_OUT = male pin header, 1 pin [form="♂ (male)"]  # not connected
  sys_count_OUT = male pin header, 4 pins [form="♂ (male)"]  # not connected
  VCC_prev = male pin header, 1 pin [form="♂ (male)"]  # not connected
  CLK_in = female pin header, 1 pin [form="♀ (female)"]
  ~W/S_in = female pin header, 1 pin [form="♀ (female)"]
  pedal_IN = female pin header, 1 pin [form="♀ (female)"]
  count_OUT = male pin header, 4 pins [form="♂ (male)"]
  VCC_in = female pin header, 1 pin [form="♀ (female)"]  # not connected
  sys_count_IN = female pin header, 4 pins [form="♀ (female)"]  # not connected
  sys_pedals_IN = female pin header, 1 pin [form="♀ (female)"]  # not connected
  CLK_out = male pin header, 1 pin [form="♂ (male)"]
  ~W/S_out = male pin header, 1 pin [form="♂ (male)"]
  pedal_OUT = male pin header, 1 pin [form="♂ (male)"]
  VCC_next = male pin header, 1 pin [form="♂ (male)"]  # not connected
  GND_in = female pin header, 1 pin [form="♀ (female)"]  # not connected
  R12 = Resistor [tolerance=±5% resistance=10k package=THT]  # not connected
  GND_out = male pin header, 1 pin [form="♂ (male)"]  # not connected
  R13 = Resistor [tolerance=±5% resistance=10k package=THT]  # not connected
  R14 = Resistor [tolerance=±5% resistance=10k package=THT]  # not connected
  R15 = Resistor [tolerance=±5% resistance=10k package=THT]  # not connected
  R16 = Resistor [tolerance=±5% resistance=10k package=THT]  # not connected
  R17 = Resistor [tolerance=±5% resistance=10k package=THT]  # not connected
  VCC_out = male pin header, 1 pin [form="♂ (male)"]  # not connected
  R18 = Resistor [tolerance=±5% resistance=10k package=THT]  # not connected
  R19 = Resistor [tolerance=±5% resistance=10k package=THT]  # not connected
  R20 = Resistor [tolerance=±5% resistance=10k package=THT]  # not connected
  R21 = Resistor [tolerance=±5% resistance=10k package=THT]  # not connected
  R22 = Resistor [tolerance=±5% resistance=10k package=THT]  # not connected
  GND_in1 = female pin header, 1 pin [form="♀ (female)"]  # not connected
  GND_out1 = male pin header, 1 pin [form="♂ (male)"]  # not connected
  R23 = Resistor [tolerance=±5% resistance=10k package=THT]
  R24 = Resistor [tolerance=±5% resistance=10k package=THT]
  R25 = Resistor [tolerance=±5% resistance=10k package=THT]
  sys_count_IN_B = female pin header, 4 pins [form="♀ (female)"]  # not connected
  CLK_in1 = female pin header, 1 pin [form="♀ (female)"]  # not connected
  R26 = Resistor [tolerance=±5% resistance=10k package=THT]
  R27 = Resistor [tolerance=±5% resistance=10k package=THT]
  R28 = Resistor [tolerance=±5% resistance=10k package=THT]
  IC6 = IC, DIP package, 14 pins [chip_label=Inverters]
  IC7 = IC, DIP package, 14 pins [chip_label="Flip Flop"]
  IC8 = IC, DIP package, 14 pins [chip_label=NANDs]
  SN54HC3 = IC, DIP package, 16 pins [chip_label=Muxes part_number=SN54HC157]
  IC9 = IC, DIP package, 16 pins [chip_label=Adder part_number=‎CD74HC283E‎]
  R29 = Resistor [tolerance=±5% resistance=10k package=THT]
  R30 = Resistor [tolerance=±5% resistance=10k package=THT]
  VCC_out_B = male pin header, 1 pin [form="♂ (male)"]  # not connected
  R31 = Resistor [tolerance=±5% resistance=10k package=THT]
  VCC_prev1 = male pin header, 1 pin [form="♂ (male)"]
  R32 = Resistor [tolerance=±5% resistance=10k package=THT]
  SN54HC4 = IC, DIP package, 16 pins [chip_label=Muxes part_number=SN54HC157]
  R33 = Resistor [tolerance=±5% resistance=10k package=THT]
  R34 = Resistor [tolerance=±5% resistance=10k package=THT]
  CLK_out_B = male pin header, 1 pin [form="♂ (male)"]  # not connected
  sys_count_OUT_B = male pin header, 4 pins [form="♂ (male)"]  # not connected
  S2 = Toggle Switch [package=THT]
  R35 = Resistor [tolerance=±5% resistance=10k package=THT]
  pedal_OUT_B = male pin header, 1 pin [form="♂ (male)"]  # not connected
  ~W/S_out_B = male pin header, 1 pin [form="♂ (male)"]  # not connected
  sys_pedals_IN_B = female pin header, 1 pin [form="♀ (female)"]  # not connected
  R36 = Resistor [tolerance=±5% resistance=10k package=THT]
  R37 = Resistor [tolerance=±5% resistance=10k package=THT]
  pedal_IN_B = female pin header, 1 pin [form="♀ (female)"]  # not connected
  ~W/S_in1 = female pin header, 1 pin [form="♀ (female)"]  # not connected
  R38 = Resistor [tolerance=±5% resistance=10k package=THT]
  sys_pedals_OUT_B = male pin header, 1 pin [form="♂ (male)"]  # not connected
  VCC_next_B = male pin header, 1 pin [form="♂ (male)"]  # not connected
  VCC_in_B = female pin header, 1 pin [form="♀ (female)"]
  count_OUT_B = male pin header, 4 pins [form="♂ (male)"]  # not connected
  count_IN_B = female pin header, 4 pins [form="♀ (female)"]  # not connected
  GND_out_B = male pin header, 2 pins [form="♂ (male)"]  # not connected
  GND_in_B = male pin header, 2 pins [form="♂ (male)"]

nets:
  N1: IC3.pin1, count_OUT.pin2
  N2: IC3.pin3, count_IN.pin2
  N3: IC3.pin4, count_OUT.pin1
  N4: IC3.pin5, count_IN.pin1
  N5: IC3.pin10, count_OUT.pin4
  N6: IC3.pin12, count_IN.pin4
  N7: IC3.pin13, count_OUT.pin3
  N8: IC3.pin14, count_IN.pin3
  N9: IC5.pin2, ~W/S_in.pin1, ~W/S_out.pin1
  N10: IC5.pin3, pedal_IN.pin1
  N11: IC4.pin3, CLK_in.pin1, CLK_out.pin1
  N12: IC4.pin5, pedal_OUT.pin1
  N13: R23.Pin_1, R24.Pin_1, R25.Pin_1, R26.Pin_1, R27.Pin_1, R28.Pin_1, IC6.pin1, IC8.pin1, SN54HC3.pin1, IC9.pin1, R29.Pin_1, R30.Pin_1, R31.Pin_1, R32.Pin_1, SN54HC4.pin1, R33.Pin_1, R34.Pin_1, S2.L2, R36.Pin_1, R37.Pin_1, R38.Pin_1, GND_in_B.pin2
  N14: R26.Pin_0, IC9.pin3
  N15: R27.Pin_0, IC9.pin14
  N16: R28.Pin_0, IC9.pin7
  N17: IC6.pin8, IC7.pin4, IC7.pin7, IC7.pin8, IC7.pin9, IC7.pin10, IC7.pin11, IC7.pin12, IC8.pin12, SN54HC3.pin9, IC9.pin2, IC9.pin9, SN54HC4.pin9, S2.L1
  N18: IC7.pin1, R35.Pin_1
  N19: IC8.pin2, IC8.pin10
  N20: IC8.pin5, IC8.pin9
  N21: IC8.pin7, S2.COM
  N22: IC8.pin8, VCC_prev1.pin1, VCC_in_B.pin1
  N23: SN54HC3.pin8, SN54HC4.pin8
  N24: IC9.pin10, R32.Pin_0
