# Fritzing sketch pedalsAssembly2 (saved by Fritzing 0.9.3b)
perfboards: 2

parts:
  S1 = Toggle Switch [package=THT]  # not connected
  IC3 = IC, DIP package, 16 pins [chip_label=Adder part_number=‎CD74HC283E‎]
  SN54HC1 = IC, DIP package, 16 pins [chip_label=Muxes part_number=SN54HC157]  # not connected
  SN54HC2 = IC, DIP package, 16 pins [chip_label=Muxes part_number=SN54HC157]
  IC5 = IC, DIP package, 14 pins [chip_label=NANDs]  # not connected
  IC4 = IC, DIP package, 14 pins [chip_label="Flip Flop"]  # not connected
  IC2 = IC, DIP package, 14 pins [chip_label=Inverters]  # not connected
  R1 = Resistor [tolerance=±5% resistance=10k package=THT]  # not connected
  R2 = Resistor [tolerance=±5% resistance=10k package=THT]  # not connected
  R3 = Resistor [tolerance=±5% resistance=10k package=THT]  # not connected
  R4 = Resistor [tolerance=±5% resistance=10k package=THT]  # not connected
  R11 = Resistor [tolerance=±5% resistance=10k package=THT]  # not connected
  count_IN = female pin header, 4 pins [form="♀ (female)"]
  sys_pedals_OUT = male pin header, 1 pin [form="♂ (male)"]  # not connected
  sys_count_OUT = male pin header, 4 pins [form="♂ (male)"]
  VCC_prev = male pin header, 1 pin [form="♂ (male)"]  # not connected
  CLK_in = female pin header, 1 pin [form="♀ (female)"]  # not connected
  ~W/S_in = female pin header, 1 pin [form="♀ (female)"]  # not connected
  pedal_IN = female pin header, 1 pin [form="♀ (female)"]  # not connected
  count_OUT = male pin header, 4 pins [form="♂ (male)"]  # not connected
  VCC_in = female pin header, 1 pin [form="♀ (female)"]  # not connected
  sys_count_IN = female pin header, 4 pins [form="♀ (female)"]  # not connected
  sys_pedals_IN = female pin header, 1 pin [form="♀ (female)"]  # not connected
  CLK_out = male pin header, 1 pin [form="♂ (male)"]  # not connected
  ~W/S_out = male pin header, 1 pin [form="♂ (male)"]  # not connected
  pedal_OUT = male pin header, 1 pin [form="♂ (male)"]  # not connected
  VCC_next = male pin header, 1 pin [form="♂ (male)"]  # not connected
  GND_in = female pin header, 1 pin [form="♀ (female)"]  # not connected
  R12 = Resistor [tolerance=±5% resistance=10k package=THT]  # not connected
  GND_out = male pin header, 1 pin [form="♂ (male)"]  # not connected
  R13 = Resistor [tolerance=±5% resistance=10k package=THT]  # not connected
  R14 = Resistor [tolerance=±5% resistance=10k package=THT]  # not connected
  R15 = Resistor [tolerance=±5% resistance=10k package=THT]  # not connected
  R16 = Resistor [tolerance=±5% resistance=10k package=THT]  # not connected
  R17 = Resistor [tolerance=±5% resistance=10k package=THT]  # not connected
  VCC_out = male pin header, 1 pin [form="♂ (male)"]  # not connected
  R18 = Resistor [tolerance=±5% resistance=10k package=THT]  # not connected
  R19 = Resistor [tolerance=±5% resistance=10k package=THT]  # not connected
  R20 = Resistor [tolerance=±5% resistance=10k package=THT]  # not connected
  R21 = Resistor [tolerance=±5% resistance=10k package=THT]  # not connected
  R22 = Resistor [tolerance=±5% resistance=10k package=THT]  # not connected
  GND_in1 = female pin header, 1 pin [form="♀ (female)"]  # not connected
  GND_out1 = male pin header, 1 pin [form="♂ (male)"]  # not connected
  R23 = Resistor [tolerance=±5% resistance=10k package=THT]  # not connected
  R24 = Resistor [tolerance=±5% resistance=10k package=THT]  # not connected
  R25 = Resistor [tolerance=±5% resistance=10k package=THT]  # not connected
  sys_count_IN_B = female pin header, 4 pins [form="♀ (female)"]  # not connected
  CLK_in1 = female pin header, 1 pin [form="♀ (female)"]  # not connected
  R26 = Resistor [tolerance=±5% resistance=10k package=THT]
  R27 = Resistor [tolerance=±5% resistance=10k package=THT]
  R28 = Resistor [tolerance=±5% resistance=10k package=THT]
  IC6 = IC, DIP package, 14 pins [chip_label=Inverters]
  IC7 = IC, DIP package, 14 pins [chip_label="Flip Flop"]
  IC8 = IC, DIP package, 14 pins [chip_label=NANDs]
  SN54HC3 = IC, DIP package, 16 pins [chip_label=Muxes part_number=SN54HC157]
  IC9 = IC, DIP package, 16 pins [chip_label=Adder part_number=‎CD74HC283E‎]
  R29 = Resistor [tolerance=±5% resistance=10k package=THT]  # not connected
  R30 = Resistor [tolerance=±5% resistance=10k package=THT]  # not connected
  VCC_out_B = male pin header, 1 pin [form="♂ (male)"]  # not connected
  R31 = Resistor [tolerance=±5% resistance=10k package=THT]
  VCC_prev1 = male pin header, 1 pin [form="♂ (male)"]
  R32 = Resistor [tolerance=±5% resistance=10k package=THT]
  SN54HC4 = IC, DIP package, 16 pins [chip_label=Muxes part_number=SN54HC157]
  R33 = Resistor [tolerance=±5% resistance=10k package=THT]  # not connected
  R34 = Resistor [tolerance=±5% resistance=10k package=THT]  # not connected
  CLK_out_B = male pin header, 1 pin [form="♂ (male)"]  # not connected
  sys_count_OUT_B = male pin header, 4 pins [form="♂ (male)"]  # not connected
  S2 = Toggle Switch [package=THT]
  R35 = Resistor [tolerance=±5% resistance=10k package=THT]  # not connected
  pedal_OUT_B = male pin header, 1 pin [form="♂ (male)"]  # not connected
  ~W/S_out_B = male pin header, 1 pin [form="♂ (male)"]  # not connected
  sys_pedals_IN_B = female pin header, 1 pin [form="♀ (female)"]  # not connected
  R36 = Resistor [tolerance=±5% resistance=10k package=THT]  # not connected
  R37 = Resistor [tolerance=±5% resistance=10k package=THT]  # not connected
  pedal_IN_B = female pin header, 1 pin [form="♀ (female)"]  # not connected
  ~W/S_in1 = female pin header, 1 pin [form="♀ (female)"]  # not connected
  R38 = Resistor [tolerance=±5% resistance=10k package=THT]
  sys_pedals_OUT_B = male pin header, 1 pin [form="♂ (male)"]  # not connected
  VCC_next_B = male pin header, 1 pin [form="♂ (male)"]  # not connected
  VCC_in_B = female pin header, 1 pin [form="♀ (female)"]
  count_OUT_B = male pin header, 4 pins [form="♂ (male)"]  # not connected
  count_IN_B = female pin header, 4 pins [form="♀ (female)"]  # not connected
  GND_out_B = male pin header, 2 pins [form="♂ (male)"]  # not connected
  GND_in_B = male pin header, 2 pins [form="♂ (male)"]

nets:
  N1: IC3.pin3, count_IN.pin2
  N2: IC3.pin5, count_IN.pin1
  N3: IC3.pin12, count_IN.pin4
  N4: IC3.pin14, count_IN.pin3
  N5: SN54HC2.pin4, sys_count_OUT.pin1
  N6: SN54HC2.pin7, sys_count_OUT.pin2
  N7: SN54HC2.pin9, sys_count_OUT.pin3
  N8: SN54HC2.pin12, sys_count_OUT.pin4
  N9: R26.Pin_0, IC9.pin10
  N10: R26.Pin_1, R28.Pin_1, IC8.pin1, IC9.pin1, R32.Pin_1, SN54HC4.pin1, S2.L2, GND_in_B.pin2
  N11: R27.Pin_0, IC9.pin3
  N12: R28.Pin_0, IC9.pin7
  N13: IC6.pin6, SN54HC3.pin8, SN54HC4.pin8
  N14: IC6.pin7, IC8.pin14
  N15: IC6.pin8, IC7.pin4, IC7.pin7, SN54HC3.pin9, IC9.pin2
  N16: IC6.pin12, IC8.pin13
  N17: IC7.pin3, SN54HC3.pin6
  N18: IC7.pin6, IC8.pin11
  N19: IC8.pin2, IC8.pin10
  N20: IC8.pin5, IC8.pin9
  N21: IC8.pin7, S2.COM
  N22: IC8.pin8, IC8.pin12, VCC_prev1.pin1, SN54HC4.pin9, S2.L1, VCC_in_B.pin1
  N23: SN54HC3.pin1, R31.Pin_1, R38.Pin_1
  N24: IC9.pin5, SN54HC4.pin6
  N25: IC9.pin8, SN54HC4.pin3
  N26: IC9.pin13, SN54HC4.pin15
  N27: IC9.pin14, R32.Pin_0
  N28: IC9.pin15, SN54HC4.pin12
